// Logisim project 16bitregister.circ as structural Verilog: 1 circuit, main circuit main
module main (
  input  [15:0] in_1,
  input  E,
  input  clk,
  output [15:0] out_4
);

  D_Flip_Flop d_ff_1 (.clk(clk), .D(in_1[15]), .Q(out_4[15]), .en(E));  // open: Qn, preset, reset
  D_Flip_Flop d_ff_2 (.clk(clk), .D(in_1[14]), .Q(out_4[14]), .en(E));  // open: Qn, preset, reset
  D_Flip_Flop d_ff_3 (.clk(clk), .D(in_1[13]), .Q(out_4[13]), .en(E));  // open: Qn, preset, reset
  D_Flip_Flop d_ff_4 (.clk(clk), .D(in_1[12]), .Q(out_4[12]), .en(E));  // open: Qn, preset, reset
  D_Flip_Flop d_ff_5 (.clk(clk), .D(in_1[11]), .Q(out_4[11]), .en(E));  // open: Qn, preset, reset
  D_Flip_Flop d_ff_6 (.clk(clk), .D(in_1[10]), .Q(out_4[10]), .en(E));  // open: Qn, preset, reset
  D_Flip_Flop d_ff_7 (.clk(clk), .D(in_1[9]), .Q(out_4[9]), .en(E));  // open: Qn, preset, reset
  D_Flip_Flop d_ff_8 (.clk(clk), .D(in_1[8]), .Q(out_4[8]), .en(E));  // open: Qn, preset, reset
  D_Flip_Flop d_ff_9 (.clk(clk), .D(in_1[7]), .Q(out_4[7]), .en(E));  // open: Qn, preset, reset
  D_Flip_Flop d_ff_10 (.clk(clk), .D(in_1[6]), .Q(out_4[6]), .en(E));  // open: Qn, preset, reset
  D_Flip_Flop d_ff_11 (.clk(clk), .D(in_1[5]), .Q(out_4[5]), .en(E));  // open: Qn, preset, reset
  D_Flip_Flop d_ff_12 (.clk(clk), .D(in_1[4]), .Q(out_4[4]), .en(E));  // open: Qn, preset, reset
  D_Flip_Flop d_ff_13 (.clk(clk), .D(in_1[3]), .Q(out_4[3]), .en(E));  // open: Qn, preset, reset
  D_Flip_Flop d_ff_14 (.clk(clk), .D(in_1[2]), .Q(out_4[2]), .en(E));  // open: Qn, preset, reset
  D_Flip_Flop d_ff_15 (.clk(clk), .D(in_1[1]), .Q(out_4[1]), .en(E));  // open: Qn, preset, reset
  D_Flip_Flop d_ff_16 (.clk(clk), .D(in_1[0]), .Q(out_4[0]), .en(E));  // open: Qn, preset, reset
endmodule
