// Logisim project 3bitreg.circ as structural Verilog: 1 circuit, main circuit main
module main (
  input  [2:0] \input ,
  input  clk,
  input  load,
  output [2:0] out_4
);

  D_Flip_Flop d_ff_1 (.clk(clk), .D(\input [2]), .Q(out_4[2]), .en(load));  // open: Qn, preset, reset
  D_Flip_Flop d_ff_2 (.clk(clk), .D(\input [1]), .Q(out_4[1]), .en(load));  // open: Qn, preset, reset
  D_Flip_Flop d_ff_3 (.clk(clk), .D(\input [0]), .Q(out_4[0]), .en(load));  // open: Qn, preset, reset
endmodule
