// Logisim project addrout.circ as structural Verilog: 1 circuit, main circuit main
module main (
  input  [11:0] pc,
  input  ARMUX,
  input  [15:0] r1,
  output [11:0] addrout
);

  Multiplexer #(.width(12)) multiplexer_1 (.in0(pc), .in1(r1[11:0]), .out(addrout), .sel(ARMUX));  // open: en
endmodule
