// Logisim project alu.circ as structural Verilog: 2 circuits, main circuit main
module main (
  input  [3:0] aluop,
  input  [15:0] a,
  input  [15:0] b,
  input  clk,
  input  ZFLD,
  output [15:0] aluresult,
  output Zflag,
  output Carry
);

  wire and_1_out, and_2_out, and_3_out, and_4_out, comparator_1_eq, main_1_cout, main_2_cout, main_3_cout,
       main_4_cout, main_5_cout, main_6_cout, main_7_cout, main_8_cout, main_9_cout, main_10_cout,
       main_11_cout, main_12_cout, main_13_cout, main_14_cout, main_15_cout, multiplexer_2_out, not_1_out,
       not_2_out, not_3_out, undriven;
  wire [1:0] idnormal_1_s0;
  wire [15:0] multiplexer_1_out, multiplexer_3_out, not_4_out;

  idnormal idnormal_1 (.b3(aluop[3]), .b1(aluop[1]), .b0(aluop[0]), .s1(idnormal_1_s0[1]), .s0(idnormal_1_s0[0]));
  Multiplexer #(.select(2), .width(16)) multiplexer_1 (
    .in0(a), .in1({16{1'b1}}), .in2(16'h1), .out(multiplexer_1_out), .sel(idnormal_1_s0));  // open: in3, en
  Multiplexer multiplexer_2 (.in0(1'b0), .in1(1'b1), .out(multiplexer_2_out), .sel(and_1_out));  // open: en
  alu1bit_main main_1 (
    .Cin(multiplexer_2_out), .b(multiplexer_3_out[0]), .a(multiplexer_1_out[0]), .aluop(aluop),
    .Cout(main_1_cout), .aluresult(aluresult[0]));
  alu1bit_main main_2 (
    .Cin(main_1_cout), .b(multiplexer_3_out[1]), .a(multiplexer_1_out[1]), .aluop(aluop), .Cout(main_2_cout),
    .aluresult(aluresult[1]));
  alu1bit_main main_3 (
    .Cin(main_2_cout), .b(multiplexer_3_out[2]), .a(multiplexer_1_out[2]), .aluop(aluop), .Cout(main_3_cout),
    .aluresult(aluresult[2]));
  alu1bit_main main_4 (
    .Cin(main_3_cout), .b(multiplexer_3_out[3]), .a(multiplexer_1_out[3]), .aluop(aluop), .Cout(main_4_cout),
    .aluresult(aluresult[3]));
  alu1bit_main main_5 (
    .Cin(main_4_cout), .b(multiplexer_3_out[4]), .a(multiplexer_1_out[4]), .aluop(aluop), .Cout(main_5_cout),
    .aluresult(aluresult[4]));
  alu1bit_main main_6 (
    .Cin(main_5_cout), .b(multiplexer_3_out[5]), .a(multiplexer_1_out[5]), .aluop(aluop), .Cout(main_6_cout),
    .aluresult(aluresult[5]));
  alu1bit_main main_7 (
    .Cin(main_6_cout), .b(multiplexer_3_out[6]), .a(multiplexer_1_out[6]), .aluop(aluop), .Cout(main_7_cout),
    .aluresult(aluresult[6]));
  alu1bit_main main_8 (
    .Cin(main_7_cout), .b(multiplexer_3_out[7]), .a(multiplexer_1_out[7]), .aluop(aluop), .Cout(main_8_cout),
    .aluresult(aluresult[7]));
  alu1bit_main main_9 (
    .Cin(main_8_cout), .b(multiplexer_3_out[8]), .a(multiplexer_1_out[8]), .aluop(aluop), .Cout(main_9_cout),
    .aluresult(aluresult[8]));
  alu1bit_main main_10 (
    .Cin(main_9_cout), .b(multiplexer_3_out[9]), .a(multiplexer_1_out[9]), .aluop(aluop),
    .Cout(main_10_cout), .aluresult(aluresult[9]));
  alu1bit_main main_11 (
    .Cin(main_10_cout), .b(multiplexer_3_out[10]), .a(multiplexer_1_out[10]), .aluop(aluop),
    .Cout(main_11_cout), .aluresult(aluresult[10]));
  alu1bit_main main_12 (
    .Cin(main_11_cout), .b(multiplexer_3_out[11]), .a(multiplexer_1_out[11]), .aluop(aluop),
    .Cout(main_12_cout), .aluresult(aluresult[11]));
  alu1bit_main main_13 (
    .Cin(main_12_cout), .b(multiplexer_3_out[12]), .a(multiplexer_1_out[12]), .aluop(aluop),
    .Cout(main_13_cout), .aluresult(aluresult[12]));
  alu1bit_main main_14 (
    .Cin(main_13_cout), .b(multiplexer_3_out[13]), .a(multiplexer_1_out[13]), .aluop(aluop),
    .Cout(main_14_cout), .aluresult(aluresult[13]));
  alu1bit_main main_15 (
    .Cin(main_14_cout), .b(multiplexer_3_out[14]), .a(multiplexer_1_out[14]), .aluop(aluop),
    .Cout(main_15_cout), .aluresult(aluresult[14]));
  alu1bit_main main_16 (
    .Cin(main_15_cout), .b(multiplexer_3_out[15]), .a(multiplexer_1_out[15]), .aluop(aluop), .Cout(Carry),
    .aluresult(aluresult[15]));
  and and_1 (and_1_out, and_2_out, and_3_out);
  and and_2 (and_2_out, not_3_out, not_1_out);
  not not_1 (not_1_out, aluop[2]);
  not not_2 (not_2_out, aluop[1]);
  and and_3 (and_3_out, not_2_out, aluop[0]);
  not not_3 (not_3_out, aluop[3]);
  and and_4 (and_4_out, ~aluop[3], ~aluop[2], ~aluop[1], aluop[0]);  // AND_Gate
  Multiplexer #(.width(16)) multiplexer_3 (
    .in0(b), .in1(not_4_out), .out(multiplexer_3_out), .sel(and_4_out), .en(undriven));
  assign not_4_out = ~b;  // NOT_Gate not_4, 16 bits wide
  Comparator #(.width(16)) comparator_1 (.a(aluresult), .b({16{1'b0}}), .eq(comparator_1_eq));  // open: gt, lt
  D_Flip_Flop d_ff_1 (.clk(clk), .D(comparator_1_eq), .Q(Zflag), .en(ZFLD));  // open: Qn, preset, reset
endmodule

module idnormal (
  input  b3,
  input  b1,
  input  b0,
  output s1,
  output s0
);

  wire not_1_out;

  and and_1 (s1, b3, b1, not_1_out);
  not not_1 (not_1_out, b0);
  and and_2 (s0, b3, b1, b0);
endmodule
