// Logisim project alu1bit.circ as structural Verilog: 1 circuit, main circuit main
module main (
  input  Cin,
  input  a,
  input  b,
  input  [3:0] aluop,
  output Cout,
  output aluresult
);

  wire and_1_out, and_2_out, and_3_out, not_1_out, or_1_out, xor_1_out, xor_2_out, xor_3_out;

  xor xor_1 (xor_1_out, a, b);
  and and_1 (and_1_out, a, b);
  not not_1 (not_1_out, b);
  and and_2 (and_2_out, a, b);
  or or_1 (or_1_out, a, b);
  xor xor_2 (xor_2_out, a, b);
  xor xor_3 (xor_3_out, Cin, xor_1_out);
  and and_3 (and_3_out, Cin, xor_1_out);
  or or_2 (Cout, and_3_out, and_1_out);
  Multiplexer #(.select(4)) multiplexer_1 (
    .in0(xor_3_out), .in1(xor_3_out), .in2(and_2_out), .in3(or_1_out), .in4(xor_2_out), .in8(b),
    .in9(not_1_out), .in10(xor_3_out), .in11(xor_3_out), .out(aluresult), .sel(aluop));  // open: in5, in6, in7, in12, in13, in14, in15, en
endmodule
