// Logisim project alucontrol.circ as structural Verilog: 1 circuit, main circuit main
module main (
  input  [5:0] aluop6,
  output [3:0] aluoptoalu
);

  wire and_1_out;
  wire [3:0] bit_extender_1_out, bit_extender_2_out;

  assign bit_extender_1_out = {{1{1'b0}}, aluop6[5:3]};  // Bit_Extender bit_extender_1
  assign bit_extender_2_out = {{1{1'b1}}, aluop6[2:0]};  // Bit_Extender bit_extender_2
  and and_1 (and_1_out, aluop6[4], aluop6[5]);
  Multiplexer #(.width(4)) multiplexer_1 (
    .in0(bit_extender_1_out), .in1(bit_extender_2_out), .out(aluoptoalu), .sel(and_1_out));  // open: en
endmodule
