// Logisim project controlunit.circ as structural Verilog: 1 circuit, main circuit main
module main (
  input  [2:0] snext,
  output PCINC,
  output ARMUX,
  output PCLD,
  output ZFLD,
  output IRLD,
  output MUX,
  output REGLD,
  output MEMLD
);

  wire and_6_out, and_7_out, and_8_out, and_9_out, and_10_out, not_1_out, not_2_out, not_3_out, not_4_out,
       not_5_out, not_6_out, not_7_out, not_8_out, not_9_out, not_10_out, not_11_out, not_12_out, not_13_out;

  not not_1 (not_1_out, snext[2]);
  not not_2 (not_2_out, snext[1]);
  not not_3 (not_3_out, snext[2]);
  not not_4 (not_4_out, snext[1]);
  and and_1 (ZFLD, snext[2], snext[1]);
  not not_5 (not_5_out, snext[1]);
  not not_6 (not_6_out, snext[0]);
  not not_7 (not_7_out, snext[2]);
  not not_8 (not_8_out, snext[1]);
  not not_9 (not_9_out, snext[0]);
  not not_10 (not_10_out, snext[2]);
  not not_11 (not_11_out, snext[1]);
  not not_12 (not_12_out, snext[0]);
  not not_13 (not_13_out, snext[2]);
  and and_2 (PCINC, not_1_out, not_2_out);
  and and_3 (ARMUX, not_3_out, snext[1]);
  and and_4 (PCLD, snext[2], not_4_out);
  and and_5 (IRLD, not_5_out, not_6_out);
  and and_6 (and_6_out, not_7_out, not_8_out, snext[0]);
  and and_7 (and_7_out, snext[1], not_9_out);
  and and_8 (and_8_out, not_10_out, not_11_out, snext[0]);
  and and_9 (and_9_out, snext[1], not_12_out);
  and and_10 (and_10_out, snext[2], snext[1]);
  and and_11 (MEMLD, not_13_out, snext[1], snext[0]);
  or or_1 (MUX, and_6_out, and_7_out);
  or or_2 (REGLD, and_8_out, and_9_out, and_10_out);
endmodule
