// Logisim project cpu.circ as structural Verilog: 2 circuits, main circuit main
module main (
  output [11:0] out_1,
  output [11:0] out_2,
  output [11:0] out_3
);

  wire ARMUX, clk, cout, hex_1_a, hex_1_b, hex_1_c, hex_1_d, hex_1_e, hex_1_f, hex_1_g, hex_2_a, hex_2_b,
       hex_2_c, hex_2_d, hex_2_e, hex_2_f, hex_2_g, hex_3_a, hex_3_b, hex_3_c, hex_3_d, hex_3_e, hex_3_f,
       hex_3_g, hex_4_a, hex_4_b, hex_4_c, hex_4_d, hex_4_e, hex_4_f, hex_4_g, IRLD, MEMLD, MUX, PCINC, PCLD,
       pcoverflow, REGLD, ZFlag, ZFLD;
  wire [2:0] destreg, op, opcode, snext, src1, src2;
  wire [3:0] aluop;
  wire [5:0] _6bitaluop;
  wire [11:0] instdata, jmpaddr;
  wire [15:0] aluresult, instreg, main_7_reg0toss, memdataread, r1, r2, regwriteinput;

  alu_main main_1 (
    .a(r1), .ZFLD(ZFLD), .aluop(aluop), .aluresult(aluresult), .b(r2), .Zflag(ZFlag), .Carry(cout), .clk(clk));
  controlunit_main main_2 (
    .PCINC(PCINC), .ARMUX(ARMUX), .PCLD(PCLD), .ZFLD(ZFLD), .IRLD(IRLD), .MUX(MUX), .REGLD(REGLD),
    .MEMLD(MEMLD), .snext(snext));
  instructionregister_main main_3 (.instruction(memdataread), .clk(clk), .IRLD(IRLD), .instreg(instreg));
  ram_main main_4 (.address(out_2), .datastore(r1), .MEMLD(MEMLD), .clk(clk), .dataread(memdataread));
  BitSelector #(.width(16), .group(12)) bitselector_1 (.in(r2), .out(out_3), .sel(1'b0));
  Clock clock_1 (.out(clk));
  addrout_main main_5 (.pc(out_1), .ARMUX(ARMUX), .r1(r1), .addrout(out_2));
  alucontrol_main main_6 (.aluop6(_6bitaluop), .aluoptoalu(aluop));
  Multiplexer #(.width(12)) multiplexer_1 (.in0(out_1), .in1(out_3), .out(out_2), .en(ARMUX));  // open: sel
  regbank_main main_7 (
    .\input (regwriteinput), .clk(clk), .destreg(destreg), .REGLD(REGLD), .src1(src1), .src2(src2),
    .reg1(r1), .reg2(r2), .reg0toss(main_7_reg0toss));
  pcunit_main main_8 (.jmpaddr(jmpaddr), .clk(clk), .pcoverflow(pcoverflow), .PCLD(PCLD), .pc(out_1), .PCINC(PCINC));
  datareceiver_main main_9 (.Din(memdataread), .op(op), .inst(instdata));
  _7_Segment_Display u_7_segment_display_1 (
    .g(hex_1_g), .f(hex_1_f), .a(hex_1_a), .b(hex_1_b), .e(hex_1_e), .d(hex_1_d), .c(hex_1_c));  // open: dp
  instructiondecoder_main main_10 (
    ._16bitinstruction(instreg), .dstreg(destreg), .src1(src1), .src2(src2), ._6bitaluop(_6bitaluop),
    .opcode(opcode), .jmpaddr(jmpaddr));
  state_machine_main main_11 (.zf(ZFlag), .op(op), .clk(clk), .snext(snext));
  Multiplexer #(.width(16)) multiplexer_2 (
    .in0(aluresult), .in1(memdataread), .out(regwriteinput), .sel(MUX));  // open: en
  hex hex_1 (
    .b3(main_7_reg0toss[15]), .b2(main_7_reg0toss[14]), .b1(main_7_reg0toss[13]), .b0(main_7_reg0toss[12]),
    .a(hex_1_a), .b(hex_1_b), .c(hex_1_c), .d(hex_1_d), .e(hex_1_e), .f(hex_1_f), .g(hex_1_g));
  hex hex_2 (
    .b3(main_7_reg0toss[11]), .b2(main_7_reg0toss[10]), .b1(main_7_reg0toss[9]), .b0(main_7_reg0toss[8]),
    .a(hex_2_a), .b(hex_2_b), .c(hex_2_c), .d(hex_2_d), .e(hex_2_e), .f(hex_2_f), .g(hex_2_g));
  _7_Segment_Display u_7_segment_display_2 (
    .g(hex_2_g), .f(hex_2_f), .a(hex_2_a), .b(hex_2_b), .e(hex_2_e), .d(hex_2_d), .c(hex_2_c));  // open: dp
  hex hex_3 (
    .b3(main_7_reg0toss[7]), .b2(main_7_reg0toss[6]), .b1(main_7_reg0toss[5]), .b0(main_7_reg0toss[4]),
    .a(hex_3_a), .b(hex_3_b), .c(hex_3_c), .d(hex_3_d), .e(hex_3_e), .f(hex_3_f), .g(hex_3_g));
  _7_Segment_Display u_7_segment_display_3 (
    .g(hex_3_g), .f(hex_3_f), .a(hex_3_a), .b(hex_3_b), .e(hex_3_e), .d(hex_3_d), .c(hex_3_c));  // open: dp
  _7_Segment_Display u_7_segment_display_4 (
    .g(hex_4_g), .f(hex_4_f), .a(hex_4_a), .b(hex_4_b), .e(hex_4_e), .d(hex_4_d), .c(hex_4_c));  // open: dp
  hex hex_4 (
    .b3(main_7_reg0toss[3]), .b2(main_7_reg0toss[2]), .b1(main_7_reg0toss[1]), .b0(main_7_reg0toss[0]),
    .a(hex_4_a), .b(hex_4_b), .c(hex_4_c), .d(hex_4_d), .e(hex_4_e), .f(hex_4_f), .g(hex_4_g));

  // Other names for the same wires on the sheet: addrout[11:0] = out_2; pc[11:0] = out_1
endmodule

module hex (
  input  b3,
  input  b2,
  input  b1,
  input  b0,
  output a,
  output b,
  output c,
  output d,
  output e,
  output f,
  output g
);

  wire and_1_out, and_2_out, and_3_out, and_4_out, and_5_out, and_6_out, and_7_out, and_8_out, and_9_out,
       and_10_out, and_11_out, and_12_out, and_13_out, and_14_out, and_15_out, and_16_out, and_17_out,
       and_18_out, and_19_out, and_20_out, and_21_out, and_22_out, and_23_out, and_24_out, and_25_out,
       and_26_out, and_27_out, and_28_out, and_29_out, and_30_out, and_31_out, and_32_out, and_33_out,
       and_34_out, and_35_out, not_1_out, not_2_out, not_3_out, not_4_out, not_5_out, not_6_out, not_7_out,
       not_8_out, not_9_out, not_10_out, not_11_out, not_12_out, not_13_out, not_14_out, not_15_out,
       not_16_out, not_17_out, not_18_out, not_19_out, not_20_out, not_21_out, not_22_out, not_23_out,
       not_24_out, not_25_out, not_26_out, not_27_out, not_28_out, not_29_out, not_30_out, not_31_out,
       not_32_out, not_33_out, not_34_out, not_35_out, not_36_out, not_37_out, not_38_out, not_39_out,
       not_40_out, not_41_out, not_42_out, not_43_out;

  not not_1 (not_1_out, b2);
  and and_1 (and_1_out, not_1_out, not_2_out);
  not not_2 (not_2_out, b0);
  not not_3 (not_3_out, b3);
  and and_2 (and_2_out, not_3_out, b1);
  not not_4 (not_4_out, b3);
  and and_3 (and_3_out, not_4_out, b2, b0);
  and and_4 (and_4_out, b2, b1);
  and and_5 (and_5_out, b3, not_5_out, not_6_out);
  not not_5 (not_5_out, b2);
  not not_6 (not_6_out, b1);
  and and_6 (and_6_out, b3, not_7_out);
  not not_7 (not_7_out, b0);
  not not_8 (not_8_out, b3);
  and and_7 (and_7_out, not_8_out, not_9_out);
  not not_9 (not_9_out, b2);
  not not_10 (not_10_out, b3);
  not not_11 (not_11_out, b1);
  and and_8 (and_8_out, not_10_out, not_11_out, not_12_out);
  not not_12 (not_12_out, b0);
  not not_13 (not_13_out, b2);
  and and_9 (and_9_out, not_13_out, not_14_out);
  not not_14 (not_14_out, b0);
  not not_15 (not_15_out, b3);
  and and_10 (and_10_out, not_15_out, b1, b0);
  not not_16 (not_16_out, b1);
  and and_11 (and_11_out, b3, not_16_out, b0);
  not not_17 (not_17_out, b3);
  and and_12 (and_12_out, not_17_out, not_18_out);
  not not_18 (not_18_out, b1);
  not not_19 (not_19_out, b3);
  and and_13 (and_13_out, not_19_out, b0);
  not not_20 (not_20_out, b1);
  and and_14 (and_14_out, not_20_out, b0);
  not not_21 (not_21_out, b3);
  and and_15 (and_15_out, not_21_out, b2);
  and and_16 (and_16_out, b3, not_22_out);
  not not_22 (not_22_out, b2);
  not not_23 (not_23_out, b3);
  and and_17 (and_17_out, not_23_out, not_24_out, not_25_out);
  not not_24 (not_24_out, b2);
  not not_25 (not_25_out, b0);
  not not_26 (not_26_out, b2);
  and and_18 (and_18_out, not_26_out, b1, b0);
  and and_19 (and_19_out, b2, not_27_out, b0);
  not not_27 (not_27_out, b1);
  and and_20 (and_20_out, b2, b1, not_28_out);
  not not_28 (not_28_out, b0);
  and and_21 (and_21_out, b3, not_29_out);
  not not_29 (not_29_out, b1);
  not not_30 (not_30_out, b2);
  and and_22 (and_22_out, not_30_out, not_31_out);
  not not_31 (not_31_out, b0);
  and and_23 (and_23_out, b1, not_32_out);
  not not_32 (not_32_out, b0);
  and and_24 (and_24_out, b3, b1);
  and and_25 (and_25_out, b3, b2);
  not not_33 (not_33_out, b1);
  and and_26 (and_26_out, not_33_out, not_34_out);
  not not_34 (not_34_out, b0);
  not not_35 (not_35_out, b3);
  and and_27 (and_27_out, not_35_out, b2, not_36_out);
  not not_36 (not_36_out, b1);
  and and_28 (and_28_out, b2, not_37_out);
  not not_37 (not_37_out, b0);
  and and_29 (and_29_out, b3, not_38_out);
  not not_38 (not_38_out, b2);
  and and_30 (and_30_out, b3, b1);
  not not_39 (not_39_out, b2);
  and and_31 (and_31_out, not_39_out, b1);
  and and_32 (and_32_out, b1, not_40_out);
  not not_40 (not_40_out, b0);
  not not_41 (not_41_out, b3);
  and and_33 (and_33_out, not_41_out, b2, not_42_out);
  not not_42 (not_42_out, b1);
  and and_34 (and_34_out, b3, not_43_out);
  not not_43 (not_43_out, b2);
  and and_35 (and_35_out, b3, b0);
  or or_1 (b, and_7_out, and_8_out, and_9_out, and_10_out, and_11_out);
  or or_2 (c, and_12_out, and_13_out, and_14_out, and_15_out, and_16_out);
  or or_3 (d, and_17_out, and_18_out, and_19_out, and_20_out, and_21_out);
  or or_4 (e, and_22_out, and_23_out, and_24_out, and_25_out);
  or or_5 (f, and_26_out, and_27_out, and_28_out, and_29_out, and_30_out);
  or or_6 (g, and_31_out, and_32_out, and_33_out, and_34_out, and_35_out);
  or or_7 (a, and_1_out, and_2_out, and_3_out, and_4_out, and_5_out, and_6_out);
endmodule
