// Logisim project datareceiver.circ as structural Verilog: 1 circuit, main circuit main
module main (
  input  [15:0] Din,
  output [2:0] op,
  output [11:0] inst
);


  assign inst = Din[11:0];
  assign op = Din[14:12];
endmodule
