// Logisim project dflipflop.circ as structural Verilog: 1 circuit, main circuit main
module main (
  input  D,
  input  clk,
  input  E,
  output Q_prime,
  output Q
);

  wire main_1_q, multiplexer_1_out, not_1_out;

  Multiplexer multiplexer_1 (.in0(Q), .in1(D), .out(multiplexer_1_out), .sel(E));  // open: en
  not not_1 (not_1_out, clk);
  dlatch_main main_1 (.D(multiplexer_1_out), .Q(main_1_q), .clk(not_1_out));  // open: Q_prime
  dlatch_main main_2 (.D(main_1_q), .Q(Q), .Q_prime(Q_prime), .clk(clk));
endmodule
