// Logisim project instructiondecoder.circ as structural Verilog: 1 circuit, main circuit main
module main (
  input  [15:0] _16bitinstruction,
  output [2:0] dstreg,
  output [2:0] src1,
  output [2:0] src2,
  output [5:0] _6bitaluop,
  output [2:0] opcode,
  output [11:0] jmpaddr
);


  assign _6bitaluop = _16bitinstruction[11:6];
  assign dstreg = _16bitinstruction[2:0];
  assign jmpaddr = _16bitinstruction[11:0];
  assign opcode = _16bitinstruction[14:12];
  assign src1 = _16bitinstruction[8:6];
  assign src2 = _16bitinstruction[5:3];
endmodule
