// Logisim project instructionregister.circ as structural Verilog: 1 circuit, main circuit main
module main (
  input  [15:0] instruction,
  input  clk,
  input  IRLD,
  output [15:0] instreg
);

  _16bitregister_main main_1 (.in_1(instruction), .clk(clk), .out_4(instreg), .E(IRLD));
endmodule
