// Logisim project microprogrammedcontrolunit.circ as structural Verilog: 1 circuit, main circuit main
module main (
  input  ZF,
  input  [2:0] op,
  input  clk,
  output PCINC,
  output ARMUX,
  output PCLD,
  output ZFLD,
  output IRLD,
  output MUX,
  output REGLD,
  output MEMLD
);

  wire [1:0] and_1_out;
  wire [2:0] main_1_out_4, multiplexer_1_out, multiplexer_2_out;

  and and_1 (and_1_out[0], op[2], ~op[1], ~op[0]);  // AND_Gate
  and and_2 (and_1_out[1], ZF, and_1_out[0]);
  Multiplexer #(.width(3)) multiplexer_1 (
    .in0(3'b000), .in1(multiplexer_2_out), .out(multiplexer_1_out), .sel(IRLD));  // open: en
  Multiplexer #(.select(2), .width(3)) multiplexer_2 (
    .in0(op), .in1(3'b000), .in3(3'b101), .out(multiplexer_2_out), .sel(and_1_out));  // open: in2, en
  _3bitreg_main main_1 (.\input (multiplexer_1_out), .clk(clk), .load(1'b1), .out_4(main_1_out_4));
  ROM #(.addrWidth(3)) rom_1 (
    .addr(main_1_out_4), .data({PCINC, ARMUX, PCLD, ZFLD, IRLD, MUX, REGLD, MEMLD}), .sel(1'b1));

  // Notes on the sheet:
  //   contents of rom_1 (hex, n*v repeats v):
  //   88 86 46 41 0 20 0 12
endmodule
