// Logisim project pcunit.circ as structural Verilog: 1 circuit, main circuit main
module main (
  input  [11:0] jmpaddr,
  input  clk,
  input  PCLD,
  input  PCINC,
  output [11:0] pc,
  output pcoverflow
);

  wire or_1_out;
  wire [11:0] adder_1_out, multiplexer_1_out;

  Multiplexer #(.width(12)) multiplexer_1 (
    .in0(12'h1), .in1(jmpaddr), .out(multiplexer_1_out), .sel(PCLD));  // open: en
  Adder #(.width(12)) adder_1 (.a(pc), .b(multiplexer_1_out), .out(adder_1_out), .cin(1'b0), .cout(pcoverflow));
  _12bitregister_main pcreg (.clk(clk), .in_1(adder_1_out), .out_4(pc), .E(or_1_out));
  or or_1 (or_1_out, PCLD, PCINC);
endmodule
