// Logisim project ram.circ as structural Verilog: 1 circuit, main circuit main
module main (
  input  [11:0] address,
  input  [15:0] datastore,
  input  MEMLD,
  input  clk,
  output [15:0] dataread
);

  RAM #(.addrWidth(12), .dataWidth(16), .bus("separate")) ram_1 (
    .addr(address), .din(datastore), .data(dataread), .str(MEMLD), .clk(clk), .ld(1'b1));  // open: sel, clr
endmodule
