// Logisim project regbank.circ as structural Verilog: 1 circuit, main circuit main
module main (
  input  [15:0] \input ,
  input  clk,
  input  REGLD,
  input  [2:0] destreg,
  input  [2:0] src2,
  input  [2:0] src1,
  output [15:0] reg0toss,
  output [15:0] reg2,
  output [15:0] reg1
);

  wire and_1_out, and_2_out, and_3_out, and_4_out, and_5_out, and_6_out, and_7_out, and_8_out,
       decoder_1_out0, decoder_1_out1, decoder_1_out2, decoder_1_out3, decoder_1_out4, decoder_1_out5,
       decoder_1_out6, decoder_1_out7;
  wire [15:0] R1_out_4, R2_out_4, R3_out_4, R4_out_4, R5_out_4, R6_out_4, R7_out_4;

  Decoder #(.select(3)) decoder_1 (
    .out0(decoder_1_out0), .out1(decoder_1_out1), .out2(decoder_1_out2), .out3(decoder_1_out3),
    .out4(decoder_1_out4), .out5(decoder_1_out5), .out6(decoder_1_out6), .out7(decoder_1_out7), .sel(destreg));  // open: en
  and and_1 (and_1_out, decoder_1_out0, REGLD);
  and and_2 (and_2_out, decoder_1_out1, REGLD);
  and and_3 (and_3_out, decoder_1_out2, REGLD);
  and and_4 (and_4_out, decoder_1_out3, REGLD);
  and and_5 (and_5_out, decoder_1_out4, REGLD);
  and and_6 (and_6_out, decoder_1_out5, REGLD);
  and and_7 (and_7_out, decoder_1_out6, REGLD);
  and and_8 (and_8_out, decoder_1_out7, REGLD);
  _16bitregister_main R0 (.in_1(\input ), .clk(clk), .out_4(reg0toss), .E(and_1_out));
  _16bitregister_main R1 (.in_1(\input ), .clk(clk), .out_4(R1_out_4), .E(and_2_out));
  _16bitregister_main R2 (.in_1(\input ), .clk(clk), .out_4(R2_out_4), .E(and_3_out));
  _16bitregister_main R3 (.in_1(\input ), .clk(clk), .out_4(R3_out_4), .E(and_4_out));
  _16bitregister_main R4 (.in_1(\input ), .clk(clk), .out_4(R4_out_4), .E(and_5_out));
  _16bitregister_main R5 (.in_1(\input ), .clk(clk), .out_4(R5_out_4), .E(and_6_out));
  _16bitregister_main R6 (.in_1(\input ), .clk(clk), .out_4(R6_out_4), .E(and_7_out));
  _16bitregister_main R7 (.in_1(\input ), .clk(clk), .out_4(R7_out_4), .E(and_8_out));
  Multiplexer #(.select(3), .width(16)) multiplexer_1 (
    .in0(reg0toss), .in1(R1_out_4), .in2(R2_out_4), .in3(R3_out_4), .in4(R4_out_4), .in5(R5_out_4),
    .in6(R6_out_4), .in7(R7_out_4), .out(reg1), .sel(src1));  // open: en
  Multiplexer #(.select(3), .width(16)) multiplexer_2 (
    .in0(reg0toss), .in1(R1_out_4), .in2(R2_out_4), .in3(R3_out_4), .in4(R4_out_4), .in5(R5_out_4),
    .in6(R6_out_4), .in7(R7_out_4), .out(reg2), .sel(src2));  // open: en
endmodule
