// Logisim project srlatch.circ as structural Verilog: 1 circuit, main circuit main
module main (
  input  s,
  input  r,
  input  s_2,
  input  r_2,
  output Q,
  output Q_2
);

  wire and_1_out, nor_1_out, nor_3_out, not_1_out;

  not not_1 (not_1_out, s_2);
  nor nor_1 (nor_1_out, s, Q);
  nor nor_2 (Q, nor_1_out, r);
  nor nor_3 (nor_3_out, s_2, Q_2);
  nor nor_4 (Q_2, nor_3_out, and_1_out);
  and and_1 (and_1_out, not_1_out, r_2);
endmodule
