// Logisim project state_machine.circ as structural Verilog: 2 circuits, main circuit main
module main (
  input  clk,
  input  [2:0] op,
  input  zf,
  output [2:0] snext
);

  wire and_1_out, and_2_out, and_4_out, and_5_out, not_1_out, not_2_out, not_3_out, not_4_out, not_5_out,
       not_6_out, not_7_out, not_8_out, not_9_out, not_10_out, not_11_out;
  wire [2:0] or_1_out;

  not not_1 (not_1_out, snext[1]);
  not not_2 (not_2_out, snext[0]);
  not not_3 (not_3_out, snext[1]);
  not not_4 (not_4_out, snext[0]);
  not not_5 (not_5_out, snext[1]);
  not not_6 (not_6_out, snext[0]);
  not not_7 (not_7_out, op[1]);
  not not_8 (not_8_out, snext[1]);
  not not_9 (not_9_out, snext[0]);
  not not_10 (not_10_out, snext[1]);
  not not_11 (not_11_out, snext[0]);
  and and_1 (and_1_out, op[2], not_1_out, not_2_out, zf);
  and and_2 (and_2_out, op[2], op[0], not_3_out, not_4_out);
  and and_3 (or_1_out[1], op[1], not_5_out, not_6_out);
  and and_4 (and_4_out, not_7_out, not_8_out, not_9_out, zf);
  and and_5 (and_5_out, op[0], not_10_out, not_11_out);
  or or_1 (or_1_out[0], and_1_out, and_2_out);
  or or_2 (or_1_out[2], and_4_out, and_5_out);
  D_Flip_Flop d_ff_1 (.clk(clk), .D(or_1_out[0]), .Q(snext[2]));  // open: Qn, preset, en, reset
  D_Flip_Flop d_ff_2 (.clk(clk), .D(or_1_out[1]), .Q(snext[1]));  // open: Qn, preset, en, reset
  D_Flip_Flop d_ff_3 (.clk(clk), .D(or_1_out[2]), .Q(snext[0]));  // open: Qn, preset, en, reset
endmodule

module ssss (
  input  op2,
  input  op1,
  input  op0,
  input  s1,
  input  s0,
  input  zf,
  output s2n,
  output s1_2,
  output s0n
);

  wire and_1_out, and_2_out, and_4_out, and_5_out, not_1_out, not_2_out, not_3_out, not_4_out, not_5_out,
       not_6_out, not_7_out, not_8_out, not_9_out, not_10_out, not_11_out;

  not not_1 (not_1_out, s1);
  not not_2 (not_2_out, s0);
  not not_3 (not_3_out, s1);
  not not_4 (not_4_out, s0);
  not not_5 (not_5_out, s1);
  not not_6 (not_6_out, s0);
  not not_7 (not_7_out, op1);
  not not_8 (not_8_out, s1);
  not not_9 (not_9_out, s0);
  not not_10 (not_10_out, s1);
  not not_11 (not_11_out, s0);
  and and_1 (and_1_out, op2, not_1_out, not_2_out, zf);
  and and_2 (and_2_out, op2, op0, not_3_out, not_4_out);
  and and_3 (s1_2, op1, not_5_out, not_6_out);
  and and_4 (and_4_out, not_7_out, not_8_out, not_9_out, zf);
  and and_5 (and_5_out, op0, not_10_out, not_11_out);
  or or_1 (s2n, and_1_out, and_2_out);
  or or_2 (s0n, and_4_out, and_5_out);
endmodule
